# Fritzing sketch WallboxBasisSchaltplan (saved by Fritzing 0.9.6b)

parts:
  J1 = female pin header, 2 pins [form="♀ (female)"]
  J2 = female pin header, 2 pins [form="♀ (female)"]
  J3 = female pin header, 2 pins [form="♀ (female)"]
  J4 = female pin header, 2 pins [form="♀ (female)"]
  J5 = female pin header, 2 pins [form="♀ (female)"]  # not connected
  J6 = female pin header, 2 pins [form="♀ (female)"]
  J7 = female pin header, 2 pins [form="♀ (female)"]
  WeMos_D1_Mini1 = WeMos D1 Mini
  J8 = female pin header, 2 pins [form="♀ (female)"]  # not connected
  J9 = female pin header, 2 pins [form="♀ (female)"]  # not connected
  J10 = female pin header, 2 pins [form="♀ (female)"]  # not connected
  J12 = female pin header, 2 pins [form="♀ (female)"]  # not connected
  J13 = female pin header, 2 pins [form="♀ (female)"]  # not connected
  U1 = L9110 H-bridge module [part_number="L9110 H-bridge"]
  SG1 = Buzzer 12mm [part_number=COM-07950 package=buzzer-12mm-ns]
  J14 = female pin header, 2 pins [form="♀ (female)"]

nets (from the breadboard view):
  N1: J1.pin1, J6.pin2
  N2: J1.pin2, U1.VCC
  N3: J2.pin2, J4.pin1, J4.pin2, U1.GND, SG1.1
  N4: J3.pin1, WeMos_D1_Mini1.3V3
  N5: J3.pin2, WeMos_D1_Mini1.D2
  N6: J6.pin1, U1.MOTOR_A-B
  N7: J7.pin1, U1.MOTOR_B-B
  N8: J7.pin2, U1.MOTOR_B-A
  N9: WeMos_D1_Mini1.D5, U1.A-IA
  N10: WeMos_D1_Mini1.D6, U1.B-IB
  N11: WeMos_D1_Mini1.D7, U1.B-IA
  N12: WeMos_D1_Mini1.D8, U1.A-IB, J14.pin2
  N13: U1.MOTOR_A-A, SG1.2

notes:
  Power Supply
  GND +12 V
  RFID
  GND 3V3 SDA SCL
  LED rot (12 V)
  LED gelb (12 V)
  LED grün (12 V)
  Power Supply 12 V
  RFID
  Buzzer
  LED grün
  LED gelb
  LED rot
  D7 LEDgelb
  D6 LEDrot
  D5 Buzzer
  D8 LEDgrün
  Power Supply
  GND +5 V

custom parts:
  Buzzer 12mm: Buzzer 12mm Spark Fun Electronics SKU : Comp-Buzzer Through hole This is a small 12mm round speaker that operates around the audible 2kHz range. You can use these speakers to create simple music or user interfaces. This is not a true piezoelectric speaker but behaves similarly. Instead of a piezoelectric crystal that vibrates with an electric current, this tiny speaker uses an electromagnet to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
